# Fritzing sketch ATtinyBoard (saved by Fritzing 0.7.12b)
breadboards: 1

parts:
  IC1 = IC, DIP package, 8 pins [chip_label=IC]
  S1 = Toggle Switch [package=THT]
  J1 = female pin header, 2 pins [form="♀ (female)"]
  J2 = female pin header, 2 pins [form="♀ (female)"]
  J3 = female pin header, 2 pins [form="♀ (female)"]
  J4 = female pin header, 2 pins [form="♀ (female)"]
  J5 = female pin header, 2 pins [form="♀ (female)"]
  J6 = female pin header, 2 pins [form="♀ (female)"]
  J7 = female pin header, 2 pins [form="♀ (female)"]
  J8 = female pin header, 2 pins [form="♀ (female)"]

nets:
  N1: IC1.pin1, J1.pin2
  N2: IC1.pin2, J6.pin2
  N3: IC1.pin3, J5.pin2
  N4: IC1.pin4, J1.pin1, J4.pin2, J8.pin2
  N5: IC1.pin5, J3.pin1
  N6: IC1.pin6, J2.pin2
  N7: IC1.pin7, S1.COM, J7.pin2
  N8: IC1.pin8, J2.pin1
  N9: S1.L2, J3.pin2
